# Fritzing sketch esquematico_matrix (saved by Fritzing 1.0.1rc)
breadboards: 1

parts:
  Disp1 = 38mm 8x8 dot matrix row cathode led display with standard pcb pads
  U1 = 74HC595 SMD [package="SO16 [SMD]"]
  U2 = 74HC595 [package="DIP16 [THT]"]
  Componente1 = Arduino Uno (Rev3) - ICSP
  R1 = Resistor [tolerance=±5% resistance=1k package="1206 [SMD]"]
  R2 = Resistor [tolerance=±5% resistance=1k package="1206 [SMD]"]
  R3 = Resistor [tolerance=±5% resistance=1k package="1206 [SMD]"]
  R4 = Resistor [tolerance=±5% resistance=1k package="1206 [SMD]"]
  R5 = Resistor [tolerance=±5% resistance=1k package="1206 [SMD]"]
  R6 = Resistor [tolerance=±5% resistance=1k package="1206 [SMD]"]
  R7 = Resistor [tolerance=±5% resistance=1k package="1206 [SMD]"]
  R8 = Resistor [tolerance=±5% resistance=1k package="1206 [SMD]"]
  Componente2 = Arduino Joystick Shield

nets:
  N1: Disp1.pin_1, U2.Q7
  N2: Disp1.pin_2, U2.Q6
  N3: Disp1.pin_3, R1.Pin_1
  N4: Disp1.pin_4, U2.Q0
  N5: Disp1.pin_5, R3.Pin_1
  N6: Disp1.pin_6, U2.Q5
  N7: Disp1.pin_7, U2.Q3
  N8: Disp1.pin_8, R8.Pin_1
  N9: Disp1.pin_9, R2.Pin_1
  N10: Disp1.pin_10, R5.Pin_1
  N11: Disp1.pin_11, U2.Q4
  N12: Disp1.pin_12, R7.Pin_1
  N13: Disp1.pin_13, U2.Q2
  N14: Disp1.pin_14, U2.Q1
  N15: Disp1.pin_15, R6.Pin_1
  N16: Disp1.pin_16, R4.Pin_1
  N17: U1.Q1, R1.Pin_0
  N18: U1.Q2, R2.Pin_0
  N19: U1.Q3, R3.Pin_0
  N20: U1.Q4, R4.Pin_0
  N21: U1.Q5, R5.Pin_0
  N22: U1.Q6, R6.Pin_0
  N23: U1.Q7, R7.Pin_0
  GND: U1.GND, U1.OE, U2.GND, U2.OE, Componente1.GND
  N24: U1.Q7', U2.DS
  VCC: U1.MR, U1.VCC, U2.MR, U2.VCC, Componente2.5V
  N25: U1.SH_CP, U2.SH_CP, Componente2.D13
  N26: U1.ST_CP, U2.ST_CP, Componente2.D11
  N27: U1.DS, Componente2.D12
  N28: U1.Q0, R8.Pin_0
